# Fritzing sketch dht (saved by Fritzing 0.9.4)
breadboards: 1

parts:
  Part1 = Arduino Uno (Rev3) - ICSP
  DHT1 = Humidity and Temperature Sensor DHT11

nets:
  N1: Part1.D4, DHT1.Data-signal
  3V3: Part1.3V3, DHT1.Vcc
  N2: Part1.GND, DHT1.GND_2

notes:
  DATA PIN

custom parts:
  Humidity and Temperature Sensor DHT11: Digital relative humidity & temperature sensor DHT11
