# Fritzing sketch distance (saved by Fritzing 0.9.4)
breadboards: 1

parts:
  Part1 = Arduino Uno (Rev3) - ICSP
  J1 = Piezo Speaker
  HC-SR04_Sensor_1 = HC-SR04 Ultrasonic Distance Sensor
  LED1 = RGB LED (com. cathode, rbg) [package="5 mm [THT]"]

nets:
  N1: Part1.D10_PWM/SS, HC-SR04_Sensor_1.TRIG
  N2: Part1.D11_PWM/MOSI, HC-SR04_Sensor_1.ECHO
  N3: Part1.D12/MISO, J1.pin2
  N4: Part1.D2, LED1.blue_anode
  N5: Part1.D3_PWM, LED1.green_anode
  N6: Part1.D4, LED1.red_anode
  5V: Part1.5V, HC-SR04_Sensor_1.VCC
  GND: Part1.GND, J1.pin1, HC-SR04_Sensor_1.GND, LED1.common_cathode
